# Fritzing sketch pingpong_clock_wiring (saved by Fritzing 0.9.3b)

parts:
  U2 = ESP8266 NodeMCU LoLin module
  HLK-PM1 = HLK-PM01
  RGB_SMD_LED1 = APA102-2020 [package=2020]
  BUTTON1 = Arcade Button (red)

nets:
  N1: U2.D1, RGB_SMD_LED1.CKI
  N2: U2.D2, RGB_SMD_LED1.SDI
  N3: U2.D3, BUTTON1.no_name_yet#1
  GND: U2.GND, HLK-PM1.-Vo, RGB_SMD_LED1.GND, BUTTON1.no_name_yet#2
  VIN: U2.Vin, HLK-PM1.+Vo, RGB_SMD_LED1.VCC

custom parts:
  ESP8266 NodeMCU LoLin module: ESP8266 based NodeMCU
  APA102-2020: APA102-2020 2mm x 2mm Individually addressable LED. Note: there are at least 3 and possibly more incompatible footprints for these LEDs from different manufacturers. This particular part is for the APA Electronic Co APA-102-2020 device (data sheet at http://neon-world.com/uploads/wenjian/20apa.pdf). Check the PCB foot print of the device you have before using this part.
  Arcade Button (red): Adafruit Arcade Button (red)
